# Fritzing sketch Elektrisk kredsløb linjefølger (saved by Fritzing 0.9.3b)
breadboards: 1

parts:
  Part1 = Arduino Uno (Rev3)
  R1 = Photocell (LDR) [package=THT]
  R2 = Photocell (LDR) [package=THT]
  R3 = Photocell (LDR) [package=THT]
  R4 = Photocell (LDR) [package=THT]
  R5 = Photocell (LDR) [package=THT]
  R6 = Resistor [tolerance=±5% resistance=220 package=THT]
  R7 = Resistor [tolerance=±5% resistance=220 package=THT]
  R8 = Resistor [tolerance=±5% resistance=220 package=THT]
  R9 = Resistor [tolerance=±5% resistance=220 package=THT]
  VCC1 = Battery block 9V
  LED6 = LED - 3mm [color="Green (565nm)" current=80mA package="3 mm [THT]"]
  LED7 = LED - 3mm [color="Green (565nm)" current=80mA package="3 mm [THT]"]
  LED8 = LED - 3mm [color="Green (565nm)" current=80mA package="3 mm [THT]"]
  LED9 = LED - 3mm [color="Green (565nm)" current=80mA package="3 mm [THT]"]
  LED10 = LED - 3mm [color="Green (565nm)" current=80mA package="3 mm [THT]"]
  R11 = Resistor [tolerance=±5% resistance=220 package=THT]
  R12 = Resistor [tolerance=±5% resistance=220 package=THT]
  R13 = Resistor [tolerance=±5% resistance=220 package=THT]
  R14 = Resistor [tolerance=±5% resistance=220 package=THT]
  R15 = Resistor [tolerance=±5% resistance=220 package=THT]
  M1 = DC Motor
  M2 = DC Motor
  motorcontrollerDRI1 = motorcontrollerDRI0002
  BAT1 = Battery Holders [package=battery-aa]
  BAT2 = Battery Holders [package=battery-aa]
  BAT3 = Battery Holders [package=battery-aa]
  BAT4 = Battery Holders [package=battery-aa]
  VCC2 = Battery block 9V
  R10 = Resistor [tolerance=±5% resistance=220 package=THT]
  S1 = Toggle Switch [package=THT]

nets:
  N1: Part1.A0, R1.pin_0, R6.Pin_0
  N2: Part1.A1, R2.pin_0, R7.Pin_0
  N3: Part1.A2, R3.pin_0, R8.Pin_0
  N4: Part1.A3, R4.pin_0, R9.Pin_0
  N5: Part1.A4/SDA, R5.pin_0, R10.Pin_0
  GND: Part1.GND, R6.Pin_1, R7.Pin_1, R8.Pin_1, R9.Pin_1, LED6.cathode, LED7.cathode, LED8.cathode, LED9.cathode, LED10.cathode, motorcontrollerDRI1.GND, R10.Pin_1, S1.L1
  N6: Part1.D2, motorcontrollerDRI1.M1
  N7: Part1.D3_PWM, motorcontrollerDRI1.M2
  N8: Part1.D5_PWM, motorcontrollerDRI1.E1
  N9: Part1.D6_PWM, motorcontrollerDRI1.E2
  N10: Part1.5V, R1.pin_1, R2.pin_1, R3.pin_1, R4.pin_1, R5.pin_1
  N11: Part1.VIN, motorcontrollerDRI1.VD, VCC2.+
  N12: VCC1.-, BAT4.-, VCC2.-, S1.COM
  N13: VCC1.+, R11.Pin_0, R12.Pin_0, R13.Pin_0, R14.Pin_0, R15.Pin_0
  N14: LED6.anode, R15.Pin_1
  N15: LED7.anode, R14.Pin_1
  N16: LED8.anode, R13.Pin_1
  N17: LED9.anode, R12.Pin_1
  N18: LED10.anode, R11.Pin_1
  N19: M1.pin_1, motorcontrollerDRI1.M1+
  N20: M1.pin_2, motorcontrollerDRI1.M1-
  N21: M2.pin_1, motorcontrollerDRI1.M2+
  N22: M2.pin_2, motorcontrollerDRI1.M2-
  N23: motorcontrollerDRI1.VS, BAT1.+
  N24: BAT1.-, BAT2.+
  N25: BAT2.-, BAT3.+
  N26: BAT3.-, BAT4.+
